# Fritzing sketch Montaje (saved by Fritzing 0.9.3b)
breadboards: 1

parts:
  Componente2 = Arduino Uno (Rev3)
  M1 = DC Motor
  M2 = DC Motor
  Componente3 = Bluetooth HC-06

nets:
  N1: Componente2.A0, M2.pin_1
  N2: Componente2.A1, M2.pin_2
  N3: Componente2.A2, M1.pin_1
  N4: Componente2.A3, M1.pin_2
  N5: Componente2.D8, Componente3.RXD
  GND: Componente2.GND, Componente3.GND
  N6: Componente2.D7, Componente3.TXD
  5V: Componente2.5V, Componente3.VCC
